# Fritzing sketch NodeMCU in AP and STA mode (saved by Fritzing 0.9.3b)
circuit board: 8.46667cm x 5.64444cm
breadboards: 1

parts:
  U1 = NodeMCU V1.0
  LED1 = LED - 5mm [color="Red (633nm)" package="5 mm [THT]"]
  R1 = Resistor [tolerance=±5% resistance=220 package=THT]
  LED2 = LED - 5mm [color="Red (633nm)" package="5 mm [THT]"]
  R2 = Resistor [tolerance=±5% resistance=220 package=THT]
  S1 = Pushbutton [package="[THT]"]
  R3 = Resistor [tolerance=±5% resistance=220 package=THT]

nets:
  N1: U1.D0, S1.Pin_3, S1.Pin_4, R3.Pin_1
  N2: U1.D2, LED1.anode
  N3: U1.D3, LED2.anode
  N4: U1.GND, R1.Pin_1, R2.Pin_1, R3.Pin_0
  N5: U1.Vin, S1.Pin_1, S1.Pin_2
  N6: LED1.cathode, R1.Pin_0
  N7: LED2.cathode, R2.Pin_0

custom parts:
  NodeMCU V1.0: ESP8266 based NodeMCU

// code stored in the sketch: Untitled2.ino
#include <ESP8266WiFi.h>          //https://github.com/esp8266/Arduino
//needed for library
#include <DNSServer.h>
#include <ESP8266WebServer.h>
#include <WiFiManager.h>         //https://github.com/tzapu/WiFiManager
#define trigger D0
#define LED D2
#define power D3
void setup() {
    // put your setup code here, to run once:
    Serial.begin(115200);
    pinMode(trigger,INPUT); 
    pinMode(LED,OUTPUT); 
     pinMode(power,OUTPUT);    
    if(digitalRead(trigger) == HIGH){
    digitalWrite(power,HIGH);
    WiFiManager wifiManager;
    wifiManager.resetSettings();
    wifiManager.autoConnect("CIRCUIT DIGEST WiFi Manager");
    Serial.println("connected :)");
  }     
}
void loop() { 
  if (WiFi.status() == WL_CONNECTED)
        {
          digitalWrite(power,LOW);
          while(WiFi.status() == WL_CONNECTED){           
            digitalWrite(LED,HIGH);
            delay(500);
            digitalWrite(LED,LOW);
            delay(200);   
          }              
        }
        else {
          digitalWrite(LED,LOW);
        }
}
